# Fritzing sketch heating_plate (saved by Fritzing 0.9.10b)
breadboards: 1

parts:
  UNO = Arduino Uno (Rev3) - ICSP
  Q1 = TRANSISTOR_NPN [package=sot89]
  U1 = RELAY [package=OJ]
  Warming_Plate = Resistor [tolerance=±5% power=30W resistance=450 package=THT]
  F1 = FUSE [package=fuse_5mm]
  S1 = Momentary Switch [package=tactile-pth]
  S2 = Momentary Switch [package=tactile-pth]
  R1 = Resistor [tolerance=±5% power=0.25 resistance=10k package=THT]
  R2 = Resistor [tolerance=±5% power=0.25 resistance=10k package=THT]
  R3 = Resistor [tolerance=±5% power=0.25 resistance=10k package=THT]
  U2 = SWITCH-SPST-2 [package=r_sw_th]
  U3 = LCD-16X2 [package=lcd-16x2]
  U5 = POT [knob_status=50% power=0.5W package=pot_mammoth]

nets:
  N1: UNO.A0, R3.Pin_1, U2.O
  N2: UNO.A1, S1.3, S1.4, R2.Pin_1
  SDI: UNO.ICSP_MOSI
  GND/Ground: UNO.GND, Q1.E, R1.Pin_0, R2.Pin_0, R3.Pin_0, U3.VSS, U3.R_W, U3.K, U5.A
  N3: UNO.D8, U3.E
  N4: UNO.D9_PWM, U3.RS
  CS: UNO.D10_PWM/SS
  SDD: UNO.D12/MISO
  SCK: UNO.D13/SCK
  N5: UNO.D2, U3.DB7
  N6: UNO.D3_PWM, U3.DB6
  N7: UNO.D4, U3.DB5
  N8: UNO.D5_PWM, U3.DB4
  N9: UNO.D6_PWM, S2.1, S2.2, R1.Pin_1
  N10: UNO.D7, Q1.B
  N11: Q1.C, U1.COIL2
  N12: U1.MAIN, F1.1
  115V: U1.NO
  5V/VIN: U1.COIL1, Warming_Plate.Pin_0, S1.1, S1.2, S2.3, S2.4, U2.P, U3.VDD, U3.A, U5.E
  N13: Warming_Plate.Pin_1, F1.2
  N14: U3.VO, U5.S

notes:
  Adafruit_MAX31856 Temp Amplifier
